# Fritzing sketch ESP32+E19+LORA+1W (saved by Fritzing 0.9.6b)

parts:
  MH-ET_Live_Minikit_for_ESP1 = MH-ET Live Minikit for ESP32
  U2 = Header 1 [package=1x01_offset]
  U3 = Header 1 [package=1x01_offset]
  U4 = Header 1 [package=1x01_offset]
  U5 = Header 1 [package=1x01_offset]
  U6 = Header 1 [package=1x01_offset]
  U7 = Header 1 [package=1x01_offset]
  U8 = Header 1 [package=1x01_offset]
  U9 = Header 1 [package=1x01_offset]
  U10 = Header 1 [package=1x01_offset]
  U11 = Header 1 [package=1x01_offset]  # not connected
  U12 = Header 1 [package=1x01_offset]  # not connected
  U13 = Header 1 [package=1x01_offset]  # not connected
  U14 = Header 1 [package=1x01_offset]  # not connected
  U15 = Header 1 [package=1x01_offset]  # not connected
  U16 = Header 1 [package=1x01_offset]
  U17 = Header 1 [package=1x01_offset]  # not connected
  U18 = Header 1 [package=1x01_offset]
  U19 = Header 1 [package=1x01_offset]
  OLED2 = OLED 128x64 I2C Monochrome Display
  GY-NEO6MV4 = SUP500F [package=sup500f]
  U20 = Header 1 [package=1x01_offset]
  U21 = Header 1 [package=1x01_offset]
  U22 = Header 1 [package=1x01_offset]
  U23 = Header 1 [package=1x01_offset]
  Q3 = Basic FET P-Channel [part_number=IRF4905 package="DPak [SMD]"]
  D3 = Schottky Diode [part_number=1N5819 package="300 mil [THT]"]
  R14 = Resistor [tolerance=±5% resistance=39k package="0603 [SMD]"]
  C10 = Ceramic Capacitor [capacitance=47µF voltage=35V package="100 mil [THT, multilayer]"]
  C11 = Ceramic Capacitor [capacitance=10µF voltage=35V package="100 mil [THT, multilayer]"]
  C12 = Ceramic Capacitor [capacitance=100nF voltage=35V package="100 mil [THT, multilayer]"]
  MOD2 = MT3608 Boost No usb
  TP2 = TP4056 [chip_label=TP4056 package="DIP (Dual Inline) [THT]"]
  BAT2 = Battery Holders [package=lipo-1100mAh]
  L2 = Inductors [package=cdrh2d09]
  S1 = Square Pushbutton
  R15 = Resistor [tolerance=±5% power=0.25 resistance=120k package=THT]
  R16 = Resistor [tolerance=±5% power=0.25 resistance=120k package=THT]
  S2 = Toggle Switch [package=THT]
  CONN1 = USB connector [package=THT]
  CONN2 = USB connector [package=THT]
  OLED3 = OLED 128x64 I2C Monochrome Display
  U24 = Header 1 [package=1x01_offset]
  U25 = Header 1 [package=1x01_offset]
  U26 = Header 1 [package=1x01_offset]
  U27 = Header 1 [package=1x01_offset]

nets:
  GND: MH-ET_Live_Minikit_for_ESP1.GND, U9.1, OLED2.GND, GY-NEO6MV4.RX-I, U22.1, C10.0, C11.0, C12.0, MOD2.IN_(-), MOD2.OUT_(-), TP2.pin6, S1.leg0, R16.Pin_0, OLED3.GND, U27.1
  N1: MH-ET_Live_Minikit_for_ESP1.IO35, R15.Pin_1, R16.Pin_1
  N2: MH-ET_Live_Minikit_for_ESP1.TMS, U19.1
  N3: MH-ET_Live_Minikit_for_ESP1.IO18, U4.1
  N4: MH-ET_Live_Minikit_for_ESP1.IO19, U2.1
  N5: MH-ET_Live_Minikit_for_ESP1.IO23, U5.1
  N6: MH-ET_Live_Minikit_for_ESP1.IO5, U7.1
  VDD: MH-ET_Live_Minikit_for_ESP1.3.3V, U3.1, OLED2.VDD, GY-NEO6MV4.VCC, U20.1, OLED3.VDD, U24.1
  N7: MH-ET_Live_Minikit_for_ESP1.IO22, OLED2.SCK, U21.1, OLED3.SCK, U25.1
  N8: MH-ET_Live_Minikit_for_ESP1.IO21, OLED2.SDA, U23.1, OLED3.SDA, U26.1
  N9: MH-ET_Live_Minikit_for_ESP1.IO16, GY-NEO6MV4.TX-O
  N10: MH-ET_Live_Minikit_for_ESP1.VCC, U10.1, C10.1, L2.1
  N11: MH-ET_Live_Minikit_for_ESP1.TDO, S1.leg1
  N12: MH-ET_Live_Minikit_for_ESP1.IO27, U18.1
  N13: MH-ET_Live_Minikit_for_ESP1.IO25, U6.1
  N14: MH-ET_Live_Minikit_for_ESP1.IO32, U8.1
  N15: MH-ET_Live_Minikit_for_ESP1.TDI, U16.1
  N16: Q3.Gate, D3.anode, R14.Pin_1, TP2.pin1, CONN1.5V
  N17: Q3.drain, TP2.pin3
  N18: Q3.source, D3.cathode, S2.L2
  N19: R14.Pin_0, TP2.pin2
  N20: C11.1, C12.1, MOD2.OUT_(+), L2.2
  N21: MOD2.IN_(+), S2.COM
  N22: TP2.pin4, BAT2.+, R15.Pin_0
  N23: TP2.pin5, BAT2.-
  N24: CONN1.d-, CONN2.d-
  N25: CONN1.d+, CONN2.d+
  GND_2: CONN1.GND, CONN1.chassis6, CONN2.GND

notes:
  +5V power
  GND
  GPIO
  // RADIO
  #define RADIO_SCLK_PIN 18
  #define RADIO_MISO_PIN 19
  #define RADIO_MOSI_PIN 23
  #define RADIO_CS_PIN 5
  #define RADIO_RST_PIN 27
  #define RADIO_DIO1_PIN 12 TDI
  #define RADIO_BUSY_PIN 14 TMS
  #define RADIO_RXEN 32
  #define RADIO_TXEN 25
  // GPS
  #define GPS_RX 17
  #define GPS_TX 16
  // Display
  #define OLED_SDA 21
  #define OLED_SCL 22
  #define OLED_RST -1
  // OTHER
  #define BUTTON_PIN 15 TDO
  #define BATTERY_PIN 35
  GND
  D5
  D4
  D3
  D2
  D1
  D0
  RST
  GND
  RXEN
  TXEN
  CS
  SDI
  SDO
  SCK
  3.3V
  5V
  GND
  VCC GND SCL SDA
  GND VCC SCL SDA

custom parts:
  MH-ET Live Minikit for ESP32: MH-ET Live Minikit for ESP32 ( http://mh.nodebb.com/topic/8/mh-et-live-minikit-for-esp32/2/) PCB footprint is invalid.
  MT3608 Boost No usb: Chip- MT3608 / B6289 DC to DC step up, power booster module. With adjustable output voltage. Current- 2A . || Input voltage- 2V-24V || Output voltage- 5V-28V Input interface- Inversed polarity- NO. || Led indicator- No.
  TP4056: A DIP stand-in part for whatever IC you want. With 6 pins on a 300mil dual inline package (DIP) footprint.
