# Fritzing sketch ESP32+LORA+GPS+OLED (saved by Fritzing 0.9.6b)

parts:
  MH-ET_Live_Minikit_for_ESP1 = MH-ET Live Minikit for ESP32
  GY-NEO6MV3 = SUP500F [package=sup500f]
  J5 = female pin header, 2 pins [form="♀ (female)" part_number="TX RX"]
  S1 = Pushbutton [package="[SMD]"]
  OLED1 = OLED 128x64 I2C Monochrome Display
  Q1 = Basic FET P-Channel [package="TO220 [THT]"]
  U1 = RELAY [package=relay-g5q]
  JP1 = Jumper [package=sj_2s-no]
  M1 = Osoyoo SX1278-ra-02

nets:
  GND: MH-ET_Live_Minikit_for_ESP1.GND, GY-NEO6MV3.RX-I, S1.Pin_1, S1.Pin_2, OLED1.GND, M1.GND
  N1: MH-ET_Live_Minikit_for_ESP1.IO34, GY-NEO6MV3.TX-O, J5.pin2
  N2: MH-ET_Live_Minikit_for_ESP1.TMS, M1.DIO1
  N3: MH-ET_Live_Minikit_for_ESP1.IO18, M1.SCK
  N4: MH-ET_Live_Minikit_for_ESP1.IO19, M1.MISO
  N5: MH-ET_Live_Minikit_for_ESP1.IO23, M1.MOSI
  N6: MH-ET_Live_Minikit_for_ESP1.IO5, M1.NSS
  3.3V: MH-ET_Live_Minikit_for_ESP1.3.3V, GY-NEO6MV3.VCC, OLED1.VDD, M1.3.3V
  N7: MH-ET_Live_Minikit_for_ESP1.TCK, M1.RST
  N8: MH-ET_Live_Minikit_for_ESP1.IO22, OLED1.SCK
  N9: MH-ET_Live_Minikit_for_ESP1.IO21, OLED1.SDA
  N10: MH-ET_Live_Minikit_for_ESP1.TDI, M1.DIO0
  N11: MH-ET_Live_Minikit_for_ESP1.IO4, Q1.gate
  N12: GY-NEO6MV3.GND, J5.pin1
  N13: Q1.drain, U1.NC
  N14: Q1.source, JP1.2
  N15: U1.COIL1, JP1.1

notes:
  NEO6M wire color ESP32
  TX yellow 34 RX
  RX orange 12 TX
  Service Button
  GPIO14 on D1 Mini
  GPIO38 on TBEAM
  128 x 64 OLED SSD1306
  OLED wire color ESP32
  SDA purple 21
  SCL blue 22
  +5V power
  GND
  #ifdef WEMOS_D1_R32_RA02
  #define RADIO_SCLK_PIN 18
  #define RADIO_MISO_PIN 19
  #define RADIO_MOSI_PIN 23
  #define RADIO_CS_PIN (NSS) 5
  #define RADIO_BUSY_PIN(DIO0) 12
  #define RADIO_RST_PIN 13
  #define RADIO_DIO1_PIN 14
  #define OLED_SDA 21
  #define OLED_SCL 22
  #define OLED_RST 36
  #endif [write your note here]

custom parts:
  MH-ET Live Minikit for ESP32: MH-ET Live Minikit for ESP32 ( http://mh.nodebb.com/topic/8/mh-et-live-minikit-for-esp32/2/) PCB footprint is invalid.
  Osoyoo SX1278-ra-02: Osoyoo Long Distance wireless transceiver Uart LoRa Module.
